// Digital circuit Bono_diagrama.dig as structural Verilog
module Bono_diagrama (
  input  [3:0] A,
  input  negA,
  input  [3:0] B,
  input  negB,
  input  in_5
);

  wire not_1_out;
  wire [0:0] add_3_s_2;
  wire [3:0] u_bin_bcd_decenas, u_bin_bcd_unidades;
  wire [4:0] add_3_s, add_4_s, xor_3_out;
  wire [5:0] add_1_s, add_2_s, xor_1_out, xor_2_out;
  wire [6:0] u_bcd_7s_2_seg, u_bcd_7s_seg;

  assign xor_1_out = {2'b00, A} ^ {6{negA}};  // XOr xor_1, 6 bits wide
  assign xor_2_out = {2'b00, B} ^ {6{negB}};  // XOr xor_2, 6 bits wide
  Add #(.Bits(6)) add_1 (.a(xor_1_out), .b({{5{1'b0}}, negA}), .c_i(1'b0), .s(add_1_s));  // open: c_o
  Add #(.Bits(6)) add_2 (.a(xor_2_out), .b({{5{1'b0}}, negB}), .c_i(1'b0), .s(add_2_s));  // open: c_o
  Add #(.Bits(6)) add_3 (.a(add_1_s), .b(add_2_s), .c_i(1'b0), .s({add_3_s_2[0], add_3_s}));  // open: c_o
  assign xor_3_out = add_3_s ^ {5{add_3_s_2[0]}};  // XOr xor_3, 5 bits wide
  Add #(.Bits(5)) add_4 (.a(xor_3_out), .b({4'b0000, add_3_s_2[0]}), .c_i(1'b0), .s(add_4_s));  // open: c_o
  bin_bcd #(.applicationType("IVERILOG"), .CodeFile("/home/krxs/Escritorio/Lab Digital/Bono/bin_bcd.v")) u_bin_bcd (
    .mag(add_4_s), .decenas(u_bin_bcd_decenas), .unidades(u_bin_bcd_unidades));
  not not_1 (not_1_out, add_3_s_2[0]);
  bcd_7s #(.applicationType("IVERILOG"), .CodeFile("/home/krxs/Escritorio/Lab Digital/Bono/bcd_7s.v")) u_bcd_7s (
    .digito(u_bin_bcd_decenas), .seg(u_bcd_7s_seg));
  bcd_7s #(.applicationType("IVERILOG"), .CodeFile("/home/krxs/Escritorio/Lab Digital/Bono/bcd_7s.v")) u_bcd_7s_2 (
    .digito(u_bin_bcd_unidades), .seg(u_bcd_7s_2_seg));
  Seven_Seg #(.commonConnectionType("anode"), .commonCathode("true")) seven_seg_1 (
    .a(in_5), .b(in_5), .c(in_5), .d(in_5), .e(in_5), .f(in_5), .g(not_1_out), .dp(in_5), .common(in_5));
  Seven_Seg #(.commonConnectionType("anode"), .commonCathode("true")) seven_seg_2 (
    .a(u_bcd_7s_seg[0]), .b(u_bcd_7s_seg[1]), .c(u_bcd_7s_seg[2]), .d(u_bcd_7s_seg[3]), .e(u_bcd_7s_seg[4]),
    .f(u_bcd_7s_seg[5]), .g(u_bcd_7s_seg[6]), .dp(in_5), .common(in_5));
  Seven_Seg #(.commonConnectionType("anode"), .commonCathode("true")) seven_seg_3 (
    .a(u_bcd_7s_2_seg[0]), .b(u_bcd_7s_2_seg[1]), .c(u_bcd_7s_2_seg[2]), .d(u_bcd_7s_2_seg[3]),
    .e(u_bcd_7s_2_seg[4]), .f(u_bcd_7s_2_seg[5]), .g(u_bcd_7s_2_seg[6]), .dp(in_5), .common(in_5));

  // Notes on the sheet:
  //   negA: negA = 1 convierte a A en -A para la resta
  //   negB: negB = 1 convierte a B en -B para la resta
endmodule
